# Fritzing sketch 555 flashing LED circuit (saved by Fritzing 0.9.3b)
circuit board: 3.8cm x 2.4cm
breadboards: 1

parts:
  U1 = 555 Timer [package="DIP8 [THT]"]
  R1 = Resistor [tolerance=±5% resistance=1k package=THT]
  R2 = Resistor [tolerance=±5% resistance=4.7k package=THT]
  LED1 = LED - 5mm [color="Red (633nm)" package="5 mm [THT]"]
  R3 = Resistor [tolerance=±5% resistance=470 package=THT]
  Power_plug1 = Power plug
  C1 = Electrolytic Capacitor [capacitance=0.1µF package="100 mil [THT, electrolytic]"]
  TP1 = longpad pin header, 2 pins [form="long pad"]

nets:
  GND: U1.Ground, R3.Pin_1, Power_plug1.GND, C1.-, TP1.pin2
  N1: U1.Trigger, U1.Threshold, R2.Pin_1, C1.+
  N2: U1.Output, LED1.anode, TP1.pin1
  5V: U1.Reset, U1.Vcc_Supply_Voltage, R1.Pin_0, Power_plug1.VCC
  N3: U1.Discharge, R1.Pin_1, R2.Pin_0
  N4: LED1.cathode, R3.Pin_0
